# Fritzing sketch fritzing_v1 (saved by Fritzing 1.0.0rc)
breadboards: 2

parts:
  Mod1 = Raspberry Pi Pico
  S1 = Momentary Switch [package=ksa_sealed_tac_switch]
  LED1 = smd LED [color="Red (633nm)" package="0603 [SMD]"]
  부품1 = Adafruit AHT20 Temperature and Humidity Sensor [part_number="Adafruit #4566"]
  부품2 = Adafruit Adalogger FeatherWing [part_number="Adafruit #2922"]
  S2 = SPST Switch [package=switch-spdt_kit]
  DS1 = DS18B20 1-Wire Temperature Sensor [part_number=DS18B20]
  TP1 = TP4056 [chip_label=TP4056 package="DIP (Dual Inline) [THT]"]
  R1 = Resistor [tolerance=±5% resistance=4.7k package="2010 [SMD]"]
  U1 = LIPO-2000mAh [package=lipo-2000]

nets:
  N1: Mod1.pin_3, Mod1.pin_8, Mod1.pin_13, Mod1.pin_18, Mod1.pin_23, Mod1.pin_28, Mod1.pin_33, Mod1.pin_38, Mod1.pin_42, S1.4
  N2: Mod1.pin_4, 부품1.SDA, 부품2.SCL
  N3: Mod1.pin_5, 부품1.SCL, 부품2.SDA
  N4: Mod1.pin_7, DS1.DQ, R1.Pin_0
  N5: Mod1.pin_19, LED1.anode
  N6: Mod1.pin_21, 부품2.MISO
  N7: Mod1.pin_22, 부품2.CS
  N8: Mod1.pin_24, 부품2.SCK
  N9: Mod1.pin_25, 부품2.MOSI
  N10: Mod1.pin_40, S2.S
  GND: S1.1, LED1.cathode, 부품1.GND, 부품2.GND, TP1.pin6
  VCC: 부품1.VCC, 부품2.+3V3
  N11: S2.P, TP1.pin3
  N12: DS1.VDD, R1.Pin_1
  N13: TP1.pin4, U1.+
  N14: TP1.pin5, U1.-

notes:
  PicoW http sensor

custom parts:
  Raspberry Pi Pico: Raspberry Pi Pico. Based around the RP2040 microcontroller the Pico is a low cost microcontroller device bringing Raspberry Pi quality, cost, and easy of use to the microcontroller space. Jan 2021, Split part in to two versions: tht (this one) and SMD. This one will drill holes for a .1 in header in pcb to allow plugging in the module as well as providing pads to solder the module to the top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
  Adafruit AHT20 Temperature and Humidity Sensor: The AHT20 is a nice but inexpensive temperature and humidity sensor from the same folks that brought us the DHT22. You can take sensor readings as often as you like, and it uses standard I2C so its super easy to use with any Arduino or Linux/Raspberry Pi board. This sensor has a typical accuracy of +- 2% relative humidity, and +-0.3 °C. There is only one I2C address so its not a good option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
  Adafruit Adalogger FeatherWing: This is the Adalogger FeatherWing: it adds both a battery-backed Real Time Clock and micro SD card storage to any Feather main board. This FeatherWing will make it real easy to add datalogging to any of our existing Feathers. You get both an I2C real time clock (PCF8523) with 32KHz crystal and battery backup, and a microSD socket that connects to the SPI port pins (+ extra pin for CS). Tested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
  TP4056: A DIP stand-in part for whatever IC you want. With 6 pins on a 300mil dual inline package (DIP) footprint.
